# Fritzing sketch LED-Matrix-Counter (saved by Fritzing 0.9.3b)
breadboards: 1

parts:
  Part1 = Arduino Uno (Rev3)
  Disp1 = LBT2088AH [part_number=LBT2088AH]
  R1 = Resistor [tolerance=±5% resistance=220 package=THT]
  C1 = Electrolytic Capacitor [capacitance=1μF package="0405 [SMD, electrolytic]"]
  Disp2 = LBT2088AH [part_number=LBT2088AH]

nets:
  N1: Part1.D9_PWM, R1.Pin_0
  N2: Part1.5V, Disp1.pin_3, C1.+
  N3: Part1.GND, Disp1.pin2, C1.-
  N4: Disp1.pin1, R1.Pin_1
  N5: Disp1.pin_14, Disp2.pin_14
  N6: Disp1.pin_15, Disp2.pin_15
  N7: Disp1.pin_16, Disp2.pin_16

notes:
  6.3V || 1000uF
  300-500 Ohm
  For more information about NeoPixel Matrices visit:
  https://learn.adafruit.com/adafruit-neopixel-uberguide
